# Fritzing sketch Project_SmartPlantWateringSystem (saved by Fritzing 0.9.5d)

parts:
  U1 = ESP8266 NodeMCU LoLin module
  Part1 = FC-28 Soil Hygrometer Module
  Part2 = FC-28 Soil Hygrometer Module - Probe
  DHT1 = DHT11 Humitidy and Temperature Sensor (3 pins)
  Part3 = 5V Relay Module
  PIR1 = PIR sensor
  Display2 = LCD screen 16x2 IIC [part_number=101290]
  WATER_PUMP1 = water pump/motor  # not connected
  S1 = Pushbutton [package="[SMD]"]
  YL-83_-_Detection_Board1 = YL-83 Rain Sensor - Detection Board
  YL-83_-_Control_Board1 = YL-83 Rain Sensor - Control Board
  VCC1 = Battery
  LED2 = smd LED [color="Red (633nm)" package="0603 [SMD]"]  # not connected
  LED1 = smd LED [color="Red (633nm)" package="0603 [SMD]"]  # not connected

nets:
  N1: U1.D1, Display2.SCL
  N2: U1.D2, Display2.SDA
  N3: U1.D3, Part3.S
  N4: U1.D4, DHT1.Signal
  3V3: U1.3V3, Part1.VCC
  GND: U1.GND, Part1.GND, S1.Pin_3, S1.Pin_4, VCC1.-
  N5: U1.D5, PIR1.SIG
  N6: U1.D6, YL-83_-_Control_Board1.DO
  N7: U1.D7, S1.Pin_1, S1.Pin_2
  VIN: U1.Vin, Part3.VCC
  N8: U1.A0, Part1.AO
  N9: Part1.POS, Part2.POS
  N10: Part1.NEG, Part2.NEG
  N11: Part3.NOpen, VCC1.+
  N12: YL-83_-_Detection_Board1.POS, YL-83_-_Control_Board1.POS
  N13: YL-83_-_Detection_Board1.NEG, YL-83_-_Control_Board1.NEG

custom parts:
  ESP8266 NodeMCU LoLin module: ESP8266 based NodeMCU
  FC-28 Soil Hygrometer Module: The FC-28 is a soil hygrometer module that uses the Texas Instruments LM393 comparator chip to provide an analog measurement of soil humidity. The digital output is high when soil moisture is over a certain threshold, as determined by adjusting the potentiometer.
  FC-28 Soil Hygrometer Module - Probe: The FC-28 is a soil hygrometer module that uses the Texas Instruments LM393 comparator chip to provide an analog measurement of soil humidity.
  DHT11 Humitidy and Temperature Sensor (3 pins): DHT11 Humidity and Temperature Sensor (3 pins).
  5V Relay Module: 5V Relay module
  LCD screen 16x2 IIC: LCD screen with HD44780 controller enables showing text, symbols, value or anything else that comes from Croduino/Arduino. It is capable of showing 16 symbols in two lines and therefore can be used in many projects that need to send clearly visible and legible output information.. • Color of symbols: White • Backlight: Blue • Dimensions: 80 x 36 x 12 mm • Screen dimensions: 64.5 x 16 mm •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
  water pump/motor: WATER PUMP BY ARDUBLOCKTR
  YL-83 Rain Sensor - Detection Board: The YL-83 is a rain sensor that has more resistance when dry and less resistance when wet. The module runs at 5V.
  YL-83 Rain Sensor - Control Board: The YL-83 is a rain sensor that has more resistance when dry and less resistance when wet. The module runs at 5V.
  Battery: Your standard 2x 18650 battery pack (7,4 Volts)
